// Digital circuit memData.dig as structural Verilog
// Mémoire de donnée avec accès 8 ou 32bits
module memData (
  input  [31:0] A,
  input  [31:0] Din,
  input  str,
  input  ld,
  input  M8,
  input  cns,
  input  [31:0] Vm,
  output [23:0] AD,
  output [31:0] Dm,
  output strM,
  output ldM,
  output [31:0] D
);

  wire Adr0, Adr1, Adr2, Adr3, and_5_out, comparator_1_eq, comparator_1_gt, comparator_2_eq, comparator_2_lt,
       comparator_3_eq, comparator_3_gt, comparator_4_eq, comparator_4_lt, HiMem, ldMem, LowMem, or_1_out,
       or_2_out, or_3_out, or_4_out, or_5_out;
  wire [7:0] multiplexer_6_out;
  wire [31:0] bitextender_1_out, multiplexer_4_out, multiplexer_7_out, multiplexer_8_out, multiplexer_9_out,
       sub_1_s, sub_2_s;

  Decoder #(.Selector_Bits(2)) decoder_1 (.sel(A[1:0]), .out_0(Adr0), .out_1(Adr1), .out_2(Adr2), .out_3(Adr3));
  Comparator #(.Bits(32)) comparator_1 (
    .a(A), .b(32'h10010000), .gt(comparator_1_gt), .eq(comparator_1_eq));  // open: lt
  Comparator #(.Bits(32)) comparator_2 (
    .a(A), .b(32'h1200ffff), .eq(comparator_2_eq), .lt(comparator_2_lt));  // open: gt
  Comparator #(.Bits(32)) comparator_3 (
    .a(A), .b(32'h7dfff000), .gt(comparator_3_gt), .eq(comparator_3_eq));  // open: lt
  Comparator #(.Bits(32)) comparator_4 (
    .a(A), .b(32'h7fffefff), .eq(comparator_4_eq), .lt(comparator_4_lt));  // open: gt
  or or_1 (or_1_out, comparator_1_gt, comparator_1_eq);
  or or_2 (or_2_out, comparator_2_eq, comparator_2_lt);
  or or_3 (or_3_out, comparator_3_gt, comparator_3_eq);
  or or_4 (or_4_out, comparator_4_eq, comparator_4_lt);
  Multiplexer #(.Bits(8)) multiplexer_1 (.sel(Adr0), .in_0(Vm[31:24]), .in_1(Din[7:0]), .out(multiplexer_4_out[7:0]));
  Multiplexer #(.Bits(8)) multiplexer_2 (.sel(Adr1), .in_0(Vm[23:16]), .in_1(Din[7:0]), .out(multiplexer_4_out[15:8]));
  Multiplexer #(.Bits(8)) multiplexer_3 (.sel(Adr2), .in_0(Vm[15:8]), .in_1(Din[7:0]), .out(multiplexer_4_out[23:16]));
  Multiplexer #(.Bits(8)) multiplexer_4 (.sel(Adr3), .in_0(Vm[7:0]), .in_1(Din[7:0]), .out(multiplexer_4_out[31:24]));
  and and_1 (LowMem, or_1_out, or_2_out);
  and and_2 (HiMem, or_3_out, or_4_out);
  or or_5 (or_5_out, LowMem, HiMem);
  Multiplexer #(.Bits(32)) multiplexer_5 (
    .sel(M8), .in_0(Din), .in_1(multiplexer_4_out), .out({Dm[7:0], Dm[15:8], Dm[23:16], Dm[31:24]}));
  and and_3 (ldMem, or_5_out, ld);
  and and_4 (strM, or_5_out, str);
  and and_5 (and_5_out, strM, M8);
  or or_6 (ldM, and_5_out, ldMem);
  Sub #(.Bits(32)) sub_1 (.a(A), .b(32'h10010000), .c_i(1'b0), .s(sub_1_s));  // open: c_o
  Sub #(.Bits(32)) sub_2 (.a(A), .b(32'h7bfff000), .c_i(1'b0), .s(sub_2_s));  // open: c_o
  Multiplexer #(.Selector_Bits(2), .Bits(8)) multiplexer_6 (
    .sel(A[1:0]), .in_0(Vm[31:24]), .in_1(Vm[23:16]), .in_2(Vm[15:8]), .in_3(Vm[7:0]), .out(multiplexer_6_out));
  Multiplexer #(.Bits(32)) multiplexer_7 (.sel(LowMem), .in_0({32{1'b0}}), .in_1(sub_1_s), .out(multiplexer_7_out));
  Multiplexer #(.Bits(32)) multiplexer_8 (
    .sel(HiMem), .in_0(multiplexer_7_out), .in_1(sub_2_s),
    .out({multiplexer_8_out[31:26], AD, multiplexer_8_out[1:0]}));
  BitExtender #(.outputBits(32)) bitextender_1 (.in(multiplexer_6_out), .out(bitextender_1_out));
  Multiplexer #(.Bits(32)) multiplexer_9 (
    .sel(cns), .in_0(bitextender_1_out), .in_1({{24{1'b0}}, multiplexer_6_out}), .out(multiplexer_9_out));
  Multiplexer #(.Bits(32)) multiplexer_10 (
    .sel(M8), .in_0({Vm[7:0], Vm[15:8], Vm[23:16], Vm[31:24]}), .in_1(multiplexer_9_out), .out(D));

  // Other names for the same wires on the sheet: Adr[31:0] = A; b1b0[1:0] = A[1:0]; mem_8 = M8; strMem = strM

  // Notes on the sheet:
  //   A: Adresse mémoire comprise entre 0x1001000 et 0x7FFFFFFF 32 bits, default 268500992
  //   Din: Donnée à écrite
  //   AD: Adresse de la donnée depuis 0
  //   str: Enregistrement mémoire
  //   ld: lecture mémoire
  //   M8: Accès mémoire 8 bits
  //   Dm: Donnée à écrire
  //   strM: Validation écriture donnée
  //   cns: chargement non signe pour lbu
  //   ldM: Validation lecture donnée
  //   D: Donnée lue en mémoire de données
  //   Vm: Valeur lue en mémoire dans le segment de donnée
  //   Pilote mémoire données Novembre 2020
endmodule

/* Test case:
A	Din	str	ld	M8	cns	strM	ldM	AD	Dm	Vm	D	#	commentaire
0x10010000	0x31323334	1	0	0	0	1	0	0	0x34333231	x	x	#	sw mem donnée
0x10010004	0x31323334	1	0	0	0	1	0	1	0x34333231	x	x	#	sw mem donnée
0x1200FFFC	0x31323334	1	0	0	0	1	0	0x7FFFFF	0x34333231	x	x	#	sw mem donnée
0x7DFFF000	0x31323334	1	0	0	0	1	0	0x800000	0x34333231	x	x	#	sw mem pile
0x7FFFEFF8	0x31323334	1	0	0	0	1	0	0xFFFFFE	0x34333231	x	x	#	sw mem pile
0x7FFFEFFC	0x31323334	1	0	0	0	1	0	0xFFFFFF	0x34333231	x	x	#	str mem pile
0x10010000	x	0	1	0	0	0	1	0	x	0x34333231	0x31323334	#	lw mem donnée
0x10010004	x	0	1	0	0	0	1	1	x	0x34333231	0x31323334	#	lw mem donnée
0x1200FFFC	x	0	1	0	0	0	1	0x7FFFFF	x	0x34333231	0x31323334	#	lw mem donnée
0x7DFFF000	x	0	1	0	0	0	1	0x800000	x	0x34333231	0x31323334	#	lw mem pile
0x7FFFEFF8	x	0	1	0	0	0	1	0xFFFFFE	x	0x34333231	0x31323334	#	lw mem pile
0x7FFFEFFC	x	0	1	0	0	0	1	0xFFFFFF	x	0x34333231	0x31323334	#	lw mem pile
0x10010001	x	0	1	1	0	0	1	0	x	0x3435FE36	0x35	#	lb mem donnee
0x10010001	x	0	1	1	1	0	1	0	x	0x3435FE36	0x35	#	lbu mem donnee
0x10010002	x	0	1	1	0	0	1	0	x	0x3435FE36	(-2)	#	lb mem donnee
0x10010002	x	0	1	1	1	0	1	0	x	0x3435FE36	0xFE	#	lbu mem donnee
0x10010003	x	0	1	1	0	0	1	0	x	0x3435FE36	0x36	#	lb mem donnee
0x10010003	x	0	1	1	1	0	1	0	x	0x3435FE36	0x36	#	lbu mem donnee
0x1200FFFD	x	0	1	1	0	0	1	0x7FFFFF	x	0x3435FE36	0x35	#	lb mem donnee
0x1200FFFD	x	0	1	1	1	0	1	0x7FFFFF	x	0x3435FE36	0x35	#	lbu mem donnee
0x1200FFFE	x	0	1	1	0	0	1	0x7FFFFF	x	0x3435FE36	(-2)	#	lb mem donnee
0x1200FFFE	x	0	1	1	1	0	1	0x7FFFFF	x	0x3435FE36	0xFE	#	lbu mem donnee
0x1200FFFF	x	0	1	1	0	0	1	0x7FFFFF	x	0x3435FE36	0x36	#	lb mem donnee
0x1200FFFF	x	0	1	1	1	0	1	0x7FFFFF	x	0x3435FE36	0x36	#	lbu mem donnee
0x7FFFEFFD	x	0	1	1	0	0	1	0xFFFFFF	x	0x3435FE36	0x35	#	lb mem donnee
0x7FFFEFFD	x	0	1	1	1	0	1	0xFFFFFF	x	0x3435FE36	0x35	#	lbu mem donnee
0x7FFFEFFE	x	0	1	1	0	0	1	0xFFFFFF	x	0x3435FE36	(-2)	#	lb mem donnee
0x7FFFEFFE	x	0	1	1	1	0	1	0xFFFFFF	x	0x3435FE36	0xFE	#	lbu mem donnee
0x7FFFEFFF	x	0	1	1	0	0	1	0xFFFFFF	x	0x3435FE36	0x36	#	lb mem donnee
0x7FFFEFFF	x	0	1	1	1	0	1	0xFFFFFF	x	0x3435FE36	0x36	#	lbu mem donnee
0x10010000	0x31323334	1	0	1	0	1	1	0	0x34CDEF01	0xABCDEF01	x	#	sb mem donnée
0x10010001	0x31323334	1	0	1	0	1	1	0	0xAB34EF01	0xABCDEF01	x	#	sb mem donnée
0x10010002	0x31323334	1	0	1	0	1	1	0	0xABCD3401	0xABCDEF01	x	#	sb mem donnée
0x10010003	0x31323334	1	0	1	0	1	1	0	0xABCDEF34	0xABCDEF01	x	#	sb mem donnée
0x7FFFEFFC	0x31323334	1	0	1	0	1	1	0xFFFFFF	0x34CDEF01	0xABCDEF01	x	#	sb mem pile
0x7FFFEFFD	0x31323334	1	0	1	0	1	1	0xFFFFFF	0xAB34EF01	0xABCDEF01	x	#	sb mem pile
0x7FFFEFFE	0x31323334	1	0	1	0	1	1	0xFFFFFF	0xABCD3401	0xABCDEF01	x	#	sb mem pile
0x7FFFEFFF	0x31323334	1	0	1	0	1	1	0xFFFFFF	0xABCDEF34	0xABCDEF01	x	#	sb mem pile
*/
