// Digital circuit memInst.dig as structural Verilog
module memInst (
  input  [31:0] Ad,
  input  [31:0] D,
  output [31:0] Op,
  output [23:0] A
);

  wire [31:0] sub_1_s;

  Sub #(.Bits(32)) sub_1 (.a(Ad), .b(32'h400000), .c_i(1'b0), .s({sub_1_s[31:26], A, sub_1_s[1:0]}));  // open: c_o

  assign Op = {D[7:0], D[15:8], D[23:16], D[31:24]};

  // Notes on the sheet:
  //   Ad: Adresse mémoire 32 bits comprise entre 0x400000 et 0x0FFFFFFFC
  //   Op: Code instruction 32 bits
  //   D: Code instruction lu depuis la mémoire de code 32 bits
  //   A: Adresse instruction à partir de 0
  //   Pilote mémoire de d'instruction Novembre 2020
  //   1
  //   Adresse / 4
  //   6 bits inutilisés
  //   Vers la mémoire
  //   2
endmodule
