// Digital circuit ual.dig as structural Verilog
module ual (
  input  [3:0] Op,
  input  [31:0] A,
  input  [31:0] B,
  output [31:0] HI,
  output [31:0] LO,
  output [31:0] S,
  output eq_0,
  output lt_0,
  output lt__eq_0
);

  wire add_c_o, cdiv, cdivu, cmult, cmultu, sub_c_o;
  wire [0:0] slt, sltu;
  wire [31:0] add, \and , divH, divL, divuH, divuL, lui, mulH, mulL, multiplexer_2_out, multiplexer_3_out,
       multiplexer_4_out, multiplexer_5_out, multuH, multuL, \nor , \or , sll, sra, srl, sub, \xor ;

  Add #(.Bits(32)) u_add (.a(A), .b(B), .c_i(1'b0), .s(add), .c_o(add_c_o));
  Sub #(.Bits(32)) u_sub (.a(A), .b(B), .c_i(1'b0), .s(sub), .c_o(sub_c_o));
  assign \and  = A & B;  // And and_1, 32 bits wide
  assign \or  = A | B;  // Or or_1, 32 bits wide
  assign \nor  = ~(A | B);  // NOr nor_1, 32 bits wide
  assign \xor  = A ^ B;  // XOr xor_1, 32 bits wide
  Multiplexer #(.Selector_Bits(4), .Bits(32)) multiplexer_1 (
    .sel(Op), .in_0(add), .in_1(\and ), .in_2(\or ), .in_3(\nor ), .in_4(\xor ), .in_5(sll), .in_6(srl),
    .in_7(sra), .in_8(sub), .in_9(lui), .in_10({{31{1'b0}}, slt[0]}), .in_11({{31{1'b0}}, sltu[0]}),
    .in_12({32{1'b0}}), .in_13({32{1'b0}}), .in_14({32{1'b0}}), .in_15({32{1'b0}}), .out(S));
  Comparator #(.Signed("true"), .Bits(32)) comparator_1 (.a(S), .b({32{1'b0}}), .eq(eq_0), .lt(lt_0));  // open: gt
  or or_2 (lt__eq_0, eq_0, lt_0);
  BarrelShifter #(.Bits(32)) u_sll (.in(B), .shift({1'b0, A[4:0]}), .out(sll));
  BarrelShifter #(.barrelShifterMode("arithmetic"), .Bits(32), .direction("right")) u_sra (
    .in(B), .shift({1'b0, A[4:0]}), .out(sra));
  BarrelShifter #(.Bits(32), .direction("right")) u_srl (.in(B), .shift({1'b0, A[4:0]}), .out(srl));
  Comparator #(.Signed("true"), .Bits(32)) u_slt (.a(A), .b(B), .lt(slt[0]));  // open: gt, eq
  BarrelShifter #(.Bits(32)) u_lui (.in(B), .shift(6'b010000), .out(lui));
  Comparator #(.Bits(32)) u_sltu (.a(A), .b(B), .lt(sltu[0]));  // open: gt, eq
  Mul #(.Signed("true"), .Bits(32)) mult (.a(A), .b(B), .mul({mulH, mulL}));
  Mul #(.Bits(32)) multu (.a(A), .b(B), .mul({multuH, multuL}));
  Div #(.remainderPositive("false"), .Signed("true"), .Bits(32)) div (.a(A), .b(B), .q(divL), .r(divH));
  Div #(.remainderPositive("false"), .Bits(32)) divu (.a(A), .b(B), .q(divuL), .r(divuH));
  Multiplexer #(.Bits(32)) multiplexer_2 (.sel(cmultu), .in_0(mulH), .in_1(multuH), .out(multiplexer_2_out));
  Multiplexer #(.Bits(32)) multiplexer_3 (.sel(cmultu), .in_0(mulL), .in_1(multuL), .out(multiplexer_3_out));
  Multiplexer #(.Bits(32)) multiplexer_4 (.sel(cdiv), .in_0(multiplexer_2_out), .in_1(divH), .out(multiplexer_4_out));
  Multiplexer #(.Bits(32)) multiplexer_5 (.sel(cdiv), .in_0(multiplexer_3_out), .in_1(divL), .out(multiplexer_5_out));
  Multiplexer #(.Bits(32)) multiplexer_6 (.sel(cdivu), .in_0(multiplexer_4_out), .in_1(divuH), .out(HI));
  Multiplexer #(.Bits(32)) multiplexer_7 (.sel(cdivu), .in_0(multiplexer_5_out), .in_1(divuL), .out(LO));
  Decoder #(.Selector_Bits(4)) decoder_1 (
    .sel(Op), .out_12(cmult), .out_13(cmultu), .out_14(cdiv), .out_15(cdivu));  // open: out_0, out_1, out_2, out_3, out_4, out_5, out_6, out_7, out_8, out_9, out_10, out_11

  // Other names for the same wires on the sheet: dec[4:0] = A[4:0]; c1 = eq_0; c2 = lt_0; c3 = lt__eq_0
endmodule

/* Test case Test UAL:
          		Op	A	B	S	  =0	<0	<=0	 LO	HI	#	opérations
loop (NA,7)
	loop(NB,7)
		let a= (NA-4)&0xFFFFFFFF; # Nombre 32 bits
		let b= (NB-4)&0xFFFFFFFF; # Nombre 32 bits
		let operation = (a+b)&0xFFFFFFFF;
				0 	(a)	(b)  (operation)  (operation=0) (operation>>31) ((operation=0)|(operation>>31)) x x  # add
		let operation = a&b;
				1 	(a)	(b)  (operation)  (operation=0) (operation>>31) ((operation=0)|(operation>>31))  x x  # and
		let operation = a|b;
				2 	(a)	(b)  (operation)  (operation=0) (operation>>31) ((operation=0)|(operation>>31)) x x  # or
		let operation = (~(a|b))&0xFFFFFFFF;
				3 	(a)	(b)  (operation)  (operation=0) (operation>>31) ((operation=0)|(operation>>31)) x x  # nor
		let operation = a^b;
				4 	(a)	(b)  (operation)  (operation=0) (operation>>31) ((operation=0)|(operation>>31))  x x  # nor
		let operation = (b)<<(NA+1);
				5 	(NA+1)	(b)  (operation)  (operation=0) (operation>>31) ((operation=0)|(operation>>31)) x x  # sll
		let operation = (b)>>(NA+1);
				6 	(NA+1)	(b)  (operation)  (operation=0) (operation>>31) ((operation=0)|(operation>>31))  x x  # srl
		let operation = ((b<<32)>>(32+NA+1));
				7 	(NA+1)	(b)  (operation)  (operation=0) (operation>>31) ((operation=0)|(operation>>31)) x x  # sra
		let operation = a-b;
				8 	(a)	(b)  (operation)  (operation=0) (operation>>31) ((operation=0)|(operation>>31))  x x  # a-b
		let operation = (b<<16);
				9 	(a)	(b)  (operation)  (operation=0) (operation>>31) ((operation=0)|(operation>>31))  x x  # lui
		let operation = ((a-b)>>31)&1;
				10 	(a)	(b)  (operation)  (operation=0) (operation>>31) ((operation=0)|(operation>>31)) x x  # slt
		let operation = (a<b);
				11 	(a)	(b)  (operation) (operation=0) (operation>>31) ((operation=0)|(operation>>31))  x x  # sltu
		let operation = ((a<<32)>>32)*((b<<32)>>32);
				12 	(a)	(b)  x  x x x (operation&0xFFFFFFFF) ((operation>>32)&0xFFFFFFFF)  # mult
		let operation = a*b;
				13 	(a)	(b)  x  x x x (operation&0xFFFFFFFF) ((operation>>32)&0xFFFFFFFF)  # multu
				14 	(NA)	(NB+1)  x  x x x (NA/(NB+1)) (NA%(NB+1))  # div
				15 	(a)	(NB+1)  x  x x x (a/(NB+1)) (a%(NB+1))  # divu
	end loop 
end loop
*/
